# Fritzing sketch Pong (saved by Fritzing 0.9.3b)
breadboards: 3

parts:
  Composant1 = Arduino Uno (Rev3)
  Start = Pushbutton [package="[THT]"]
  R1 = Resistor [tolerance=±5% resistance=10k package=THT]
  Audio = RCA [package=rca]
  R2 = Resistor [tolerance=±5% resistance=470 package=THT]
  R3 = Resistor [tolerance=±5% resistance=1k package=THT]
  Video = RCA [package=rca]
  R4 = Rotary Potentiometer (Small) [maximum_resistance=100kΩ package=THT]
  R5 = Rotary Potentiometer (Small) [maximum_resistance=100kΩ package=THT]

nets:
  N1: Composant1.A0, R4.wiper
  N2: Composant1.A1, R5.wiper
  N3: Composant1.D9_PWM, R3.Pin_0
  N4: Composant1.D11_PWM/MOSI, Audio.SHELL
  N5: Composant1.D2, Start.Pin_3, Start.Pin_4, R1.Pin_1
  N6: Composant1.D7, R2.Pin_0
  N7: Composant1.5V, Start.Pin_1, Start.Pin_2, R4.leg2, R5.leg2
  N8: Composant1.GND, R1.Pin_0, Audio.SWITCH, Video.SWITCH, R4.leg1, R5.leg1
  N9: R2.Pin_1, R3.Pin_1, Video.SHELL
