# Fritzing sketch Roby (saved by Fritzing 0.9.0b)
breadboards: 1

parts:
  Part1 = Arduino Uno (Rev3)
  PING)))_SENSOR1 = PING))) SENSOR
  IC1 = L293D [package=THT]
  M1 = DC Motor
  M2 = DC Motor
  VCC1 = Battery block 9V
  VCC2 = Battery block 9V

nets:
  N1: Part1.D9_PWM, IC1.Enable_1
  N2: Part1.D10_PWM/SS, IC1.Enable_2
  5V: Part1.D11_PWM/MOSI, Part1.D12/MISO, Part1.5V, PING)))_SENSOR1.5V, PING)))_SENSOR1.SIGNAL
  N3: Part1.D2, IC1.In_2
  N4: Part1.D3_PWM, IC1.In_1
  N5: Part1.D4, IC1.In_3
  N6: Part1.D5_PWM, IC1.In_4
  GND: Part1.GND, PING)))_SENSOR1.GND, IC1.0V, VCC1.-, VCC2.-
  N7: Part1.VIN, VCC2.+
  N8: IC1.Out_1_(_Controlled_by_Enable_1_), M1.pin_1
  N9: IC1.Out_2_(_Controlled_by_Enable_1_), M1.pin_2
  N10: IC1.+Vmotor, IC1.+V, VCC1.+
  N11: IC1.Out_3_(_Controlled_by_Enable_2_), M2.pin_2
  N12: IC1.Out_4_(_Controlled_by_Enable_2_), M2.pin_1
